// Logisim project NUT16_v1.0.circ as structural Verilog: 4 circuits, main circuit CTRL
module main (
);

  wire alu_1_carry, ALU_enable, and_2_out, and_3_out, and_4_out, branch, clock_1_out, clock_2_out,
       clock_3_out, clock_4_out, clock_5_out, clock_6_out, clock_7_out, comparator_1_eq, comparator_2_eq,
       compare, connect, decoder_1_out0, decoder_1_out1, decoder_1_out2, decoder_1_out3, decoder_1_out4,
       decoder_1_out5, decoder_1_out6, decoder_1_out7, decoder_2_out0, decoder_2_out1, decoder_2_out2,
       decoder_2_out3, decoder_2_out4, decoder_2_out5, decoder_2_out6, decoder_2_out7, decoder_3_out0,
       decoder_3_out1, decoder_3_out2, decoder_3_out3, decoder_3_out4, decoder_3_out5, decoder_3_out6,
       decoder_3_out7, dobranch, halt, keyboard_1_avail, load_imm, load_RAM, load_reg, nor_1_out, not_1_out,
       not_2_out, not_3_out, not_4_out, or_1_out, or_2_out, port_status, read_port, set_port, size,
       write_port, write_RAM, write_reg;
  wire [2:0] bit_extender_2_out, bit_extender_3_out;
  wire [6:0] bit_extender_5_out, keyboard_1_data;
  wire [7:0] arg_reg, bit_extender_4_out, opcode, port_address, ram_1_p8, ram_1_p9, rom_2_p2, rom_2_p3;
  wire [15:0] A_q, adder_1_out, arg_data, B_q, bit_extender_1_out, bit_extender_6_out, BUS_arg1, BUS_arg2,
       BUS_result, C_q, controlled_buffer_1_out, D_q, E_q, IP, multiplexer_1_out, multiplexer_2_out,
       multiplexer_3_out, multiplexer_4_out, port_data, rom_2_p1, SBP_q, shifter_1_out, shifter_2_out, SP_q;

  or or_1 (or_1_out, write_RAM, load_RAM);
  assign bit_extender_1_out = {{15{or_1_out}}, or_1_out};  // Bit_Extender bit_extender_1
  Clock clock_1 (.out(clock_1_out));
  not not_1 (not_1_out, size);
  Multiplexer #(.width(16)) multiplexer_1 (
    .in0(BUS_arg1), .in1(shifter_1_out), .out(multiplexer_1_out), .sel(not_1_out));
  Shifter #(.width(16)) shifter_1 (.in(BUS_arg1), .\dist (4'b1000), .out(shifter_1_out));
  // ROM #(.addrWidth(16), .line("quad"), .misaligned("true")) rom_1: pin names not known; wires that end beside it: IP, opcode, arg_reg
  // ROM #(.addrWidth(16), .line("dual"), .misaligned("true")) rom_2: pin names not known; wires that end beside it: rom_2_p1, rom_2_p2, rom_2_p3
  assign rom_2_p1 = BUS_arg2 & bit_extender_1_out;  // AND_Gate and_1, 16 bits wide
  // RAM #(.addrWidth(16), .enables("line"), .line("dual"), .misaligned("true")) ram_1: pin names not known; wires that end beside it: rom_2_p1, write_RAM, 1'b1, size, clock_1_out, multiplexer_1_out[15:8], multiplexer_1_out[7:0], ram_1_p8, ram_1_p9
  CTRL ctrl_1 (
    .opcode(opcode), .load_imm(load_imm), .load_reg(load_reg), .size(size), .write_reg(write_reg),
    .write_RAM(write_RAM), .load_RAM(load_RAM), .ALU_enable(ALU_enable), .compare(compare), .branch(branch),
    .write_port(write_port), .read_port(read_port), .set_port(set_port), .halt(halt), .connect(connect));
  assign controlled_buffer_1_out = not_2_out ? {rom_2_p2, rom_2_p3} : 16'bz;  // Controlled_Buffer controlled_buffer_1
  not not_2 (not_2_out, or_2_out);
  or or_2 (or_2_out, rom_2_p1[14], rom_2_p1[15]);
  assign controlled_buffer_1_out = or_2_out ? {ram_1_p8, ram_1_p9} : 16'bz;  // Controlled_Buffer controlled_buffer_2
  not not_3 (not_3_out, size);
  Multiplexer #(.width(16)) multiplexer_2 (
    .in0(controlled_buffer_1_out), .in1(shifter_2_out), .out(multiplexer_2_out), .sel(not_3_out));
  Shifter #(.shift("lr"), .width(16)) shifter_2 (.in(controlled_buffer_1_out), .\dist (4'b1000), .out(shifter_2_out));
  assign BUS_result = load_RAM ? multiplexer_2_out : 16'bz;  // Controlled_Buffer controlled_buffer_3
  Bit_Extender #(.in_width(16), .out_width(3)) bit_extender_2 (.in(arg_data), .out(bit_extender_2_out));
  Decoder #(.select(3)) decoder_1 (
    .out0(decoder_1_out0), .out1(decoder_1_out1), .out2(decoder_1_out2), .out3(decoder_1_out3),
    .out4(decoder_1_out4), .out5(decoder_1_out5), .out6(decoder_1_out6), .out7(decoder_1_out7),
    .sel(bit_extender_2_out), .en(load_reg));
  Bit_Extender #(.out_width(3)) bit_extender_3 (.in(arg_reg), .out(bit_extender_3_out));
  Decoder #(.enable("false"), .select(3)) decoder_2 (
    .out0(decoder_2_out0), .out1(decoder_2_out1), .out2(decoder_2_out2), .out3(decoder_2_out3),
    .out4(decoder_2_out4), .out5(decoder_2_out5), .out6(decoder_2_out6), .out7(decoder_2_out7),
    .sel(bit_extender_3_out));
  Decoder #(.select(3)) decoder_3 (
    .out0(decoder_3_out0), .out1(decoder_3_out1), .out2(decoder_3_out2), .out3(decoder_3_out3),
    .out4(decoder_3_out4), .out5(decoder_3_out5), .out6(decoder_3_out6), .out7(decoder_3_out7),
    .sel(bit_extender_3_out), .en(write_reg));
  nor nor_1 (nor_1_out, decoder_3_out7, dobranch);
  Multiplexer #(.width(16)) multiplexer_3 (
    .in0(BUS_result), .in1(adder_1_out), .out(multiplexer_3_out), .sel(nor_1_out));
  not not_4 (not_4_out, halt);
  Clock clock_2 (.out(clock_2_out));
  assign BUS_result = connect ? BUS_arg2 : 16'bz;  // Controlled_Buffer controlled_buffer_4
  Register #(.width(16)) A (.D(BUS_result), .en(decoder_3_out0), .clk(clock_2_out), .Q(A_q));  // open: clr
  Register #(.width(16)) B (.D(BUS_result), .en(decoder_3_out1), .clk(clock_2_out), .Q(B_q));  // open: clr
  Register #(.width(16)) C (.D(BUS_result), .en(decoder_3_out2), .clk(clock_2_out), .Q(C_q));  // open: clr
  Register #(.width(16)) D (.D(BUS_result), .en(decoder_3_out3), .clk(clock_2_out), .Q(D_q));  // open: clr
  Register #(.width(16)) E (.D(BUS_result), .en(decoder_3_out4), .clk(clock_2_out), .Q(E_q));  // open: clr
  Register #(.width(16)) SP (.D(BUS_result), .en(decoder_3_out5), .clk(clock_2_out), .Q(SP_q));  // open: clr
  Register #(.width(16)) SBP (.D(BUS_result), .en(decoder_3_out6), .clk(clock_2_out), .Q(SBP_q));  // open: clr
  Register #(.width(16)) u_IP (.D(multiplexer_3_out), .en(not_4_out), .clk(clock_2_out), .Q(IP));  // open: clr
  Adder #(.width(16)) adder_1 (.a(IP), .b(16'h4), .out(adder_1_out));  // open: cin, cout
  assign BUS_arg1 = decoder_2_out0 ? A_q : 16'bz;  // Controlled_Buffer controlled_buffer_5
  assign BUS_arg2 = decoder_1_out0 ? A_q : 16'bz;  // Controlled_Buffer controlled_buffer_6
  assign BUS_arg1 = decoder_2_out1 ? B_q : 16'bz;  // Controlled_Buffer controlled_buffer_7
  assign BUS_arg2 = decoder_1_out1 ? B_q : 16'bz;  // Controlled_Buffer controlled_buffer_8
  assign BUS_arg1 = decoder_2_out2 ? C_q : 16'bz;  // Controlled_Buffer controlled_buffer_9
  assign BUS_arg2 = decoder_1_out2 ? C_q : 16'bz;  // Controlled_Buffer controlled_buffer_10
  assign BUS_arg1 = decoder_2_out3 ? D_q : 16'bz;  // Controlled_Buffer controlled_buffer_11
  assign BUS_arg2 = decoder_1_out3 ? D_q : 16'bz;  // Controlled_Buffer controlled_buffer_12
  assign BUS_arg1 = decoder_2_out4 ? E_q : 16'bz;  // Controlled_Buffer controlled_buffer_13
  assign BUS_arg2 = decoder_1_out4 ? E_q : 16'bz;  // Controlled_Buffer controlled_buffer_14
  assign BUS_arg1 = decoder_2_out5 ? SP_q : 16'bz;  // Controlled_Buffer controlled_buffer_15
  assign BUS_arg2 = decoder_1_out5 ? SP_q : 16'bz;  // Controlled_Buffer controlled_buffer_16
  assign BUS_arg1 = decoder_2_out6 ? SBP_q : 16'bz;  // Controlled_Buffer controlled_buffer_17
  assign BUS_arg2 = decoder_1_out6 ? SBP_q : 16'bz;  // Controlled_Buffer controlled_buffer_18
  assign BUS_arg1 = decoder_2_out7 ? IP : 16'bz;  // Controlled_Buffer controlled_buffer_19
  assign BUS_arg2 = decoder_1_out7 ? IP : 16'bz;  // Controlled_Buffer controlled_buffer_20
  assign BUS_arg2 = load_imm ? arg_data : 16'bz;  // Controlled_Buffer controlled_buffer_21
  Clock clock_3 (.out(clock_3_out));
  Bit_Extender #(.in_width(16), .out_width(8), .\type ("zero")) bit_extender_4 (
    .in(BUS_arg2), .out(bit_extender_4_out));
  Clock clock_4 (.out(clock_4_out));
  Register u_port_address (.D(bit_extender_4_out), .en(set_port), .clk(clock_4_out), .Q(port_address));  // open: clr
  assign BUS_result = read_port ? port_data : 16'bz;  // Controlled_Buffer controlled_buffer_22
  assign port_data = write_port ? multiplexer_4_out : 16'bz;  // Controlled_Buffer controlled_buffer_23
  Multiplexer #(.width(16)) multiplexer_4 (.in0(BUS_arg1), .in1(BUS_arg2), .out(multiplexer_4_out), .sel(load_imm));
  ALU alu_1 (
    .ALU_enable(ALU_enable), .opcode(opcode), .operand1(BUS_arg1), .operand2(BUS_arg2), .CLK(clock_3_out),
    .result(BUS_result), .carry(alu_1_carry));
  Pull_Resistor pull_resistor_1 (.node(port_status));
  Clock clock_5 (.out(clock_5_out));
  Clock clock_6 (.out(clock_6_out));
  CMP cmp_1 (
    .trybranch(branch), .compare(compare), .opcode(opcode), .operand1(BUS_arg1), .operand2(BUS_arg2),
    .carry(alu_1_carry), .port_ready(port_status), .CLK(clock_5_out), .dobranch(dobranch));
  Comparator comparator_1 (.a(port_address), .b({8{1'b0}}), .eq(comparator_1_eq));  // open: gt, lt
  assign port_status = comparator_1_eq ? keyboard_1_avail : 1'bz;  // Controlled_Buffer controlled_buffer_24
  Bit_Extender #(.in_width(16), .out_width(7), .\type ("zero")) bit_extender_5 (
    .in(port_data), .out(bit_extender_5_out));
  TTY tty_1 (.data(bit_extender_5_out), .clk(clock_6_out), .we(and_4_out));  // open: clr
  Comparator comparator_2 (.a(port_address), .b(8'h1), .eq(comparator_2_eq));  // open: gt, lt
  Clock clock_7 (.out(clock_7_out));
  Keyboard keyboard_1 (
    .clk(clock_7_out), .re(and_2_out), .clr(and_3_out), .avail(keyboard_1_avail), .data(keyboard_1_data));
  and and_2 (and_2_out, comparator_1_eq, read_port);
  and and_3 (and_3_out, comparator_1_eq, write_port);
  and and_4 (and_4_out, comparator_2_eq, write_port);
  assign bit_extender_6_out = {{9{1'b0}}, keyboard_1_data};  // Bit_Extender bit_extender_6
  assign port_data = and_2_out ? bit_extender_6_out : 16'bz;  // Controlled_Buffer controlled_buffer_25

  // Notes on the sheet:
  //   contents of rom_1 (hex, n*v repeats v):
  //   62 0 0 1 4 2 0 24 3 1 0 2 20 1 0 0 30 0 0 20 61 1 0 0 40 2 0 1 3a 0 0 8 ff 0 0 0 48 65 6c 6c 6f 20
  //   57 6f 72 6c 64 21 a 50 6f 67 63 68 61 6d 70 a
  //   contents of rom_2 (hex, n*v repeats v):
  //   62 0 0 1 4 2 0 24 3 1 0 2 20 1 0 0 30 0 0 20 61 1 0 0 40 2 0 1 3a 0 0 8 ff 0 0 0 48 65 6c 6c 6f 20
  //   57 6f 72 6c 64 21 a 50 6f 67 63 68 61 6d 70 a
endmodule

module CTRL (
  input  [7:0] opcode,
  output load_imm,
  output load_reg,
  output size,
  output write_reg,
  output write_RAM,
  output load_RAM,
  output ALU_enable,
  output compare,
  output branch,
  output write_port,
  output read_port,
  output set_port,
  output halt,
  output connect
);

  wire decoder_1_out0, decoder_1_out1, decoder_1_out2, decoder_1_out3, decoder_1_out4, decoder_1_out5,
       decoder_1_out15, decoder_2_out0, decoder_2_out4, decoder_2_out5, decoder_2_out6, decoder_2_out15,
       nor_1_out, or_1_out, or_2_out;

  Decoder #(.enable("false"), .select(4)) decoder_1 (
    .out0(decoder_1_out0), .out1(decoder_1_out1), .out2(decoder_1_out2), .out3(decoder_1_out3),
    .out4(decoder_1_out4), .out5(decoder_1_out5), .out15(decoder_1_out15), .sel(opcode[3:0]));  // open: out6, out7, out8, out9, out10, out11, out12, out13, out14
  Decoder #(.enable("false"), .select(4)) decoder_2 (
    .out0(decoder_2_out0), .out1(write_RAM), .out2(compare), .out3(branch), .out4(decoder_2_out4),
    .out5(decoder_2_out5), .out6(decoder_2_out6), .out15(decoder_2_out15), .sel(opcode[7:4]));  // open: out7, out8, out9, out10, out11, out12, out13, out14
  and and_1 (load_reg, opcode[0], ~branch);  // AND_Gate
  nor nor_1 (nor_1_out, decoder_1_out4, decoder_1_out5);
  or or_1 (or_1_out, decoder_1_out0, decoder_1_out1);
  or or_2 (or_2_out, decoder_2_out0, branch);
  not not_1 (load_imm, load_reg);
  or or_3 (size, decoder_1_out0, decoder_1_out1);
  or or_4 (write_reg, decoder_2_out0, read_port, ALU_enable);
  and and_2 (load_RAM, decoder_2_out0, nor_1_out);
  or or_5 (ALU_enable, decoder_2_out4, decoder_2_out5);
  and and_3 (write_port, decoder_2_out6, or_1_out);
  and and_4 (read_port, decoder_2_out6, decoder_1_out3);
  and and_5 (set_port, decoder_2_out6, decoder_1_out2);
  and and_6 (halt, decoder_2_out15, decoder_1_out15);
  and and_7 (connect, ~load_RAM, or_2_out);  // AND_Gate
endmodule

module ALU (
  input  ALU_enable,
  input  [7:0] opcode,
  input  [15:0] operand1,
  input  [15:0] operand2,
  input  CLK,
  output [15:0] result,
  output carry
);

  wire adder_1_cout, and_2_out, controlled_buffer_2_out, decoder_1_out0, decoder_1_out1, decoder_1_out2,
       decoder_1_out3, decoder_1_out4, decoder_1_out5, decoder_1_out6, decoder_1_out7, decoder_1_out8,
       decoder_1_out9, decoder_1_out10, subtractor_1_bout;
  wire [3:0] bit_extender_1_out;
  wire [15:0] adder_1_out, and_1_out, controlled_buffer_1_out, divider_1_out, divider_1_rem,
       multiplier_1_out, negator_1_out, not_1_out, or_1_out, shifter_1_out, shifter_2_out, subtractor_1_out;

  Decoder #(.enable("false"), .select(4)) decoder_1 (
    .out0(decoder_1_out0), .out1(decoder_1_out1), .out2(decoder_1_out2), .out3(decoder_1_out3),
    .out4(decoder_1_out4), .out5(decoder_1_out5), .out6(decoder_1_out6), .out7(decoder_1_out7),
    .out8(decoder_1_out8), .out9(decoder_1_out9), .out10(decoder_1_out10), .sel(opcode[4:1]));  // open: out11, out12, out13, out14, out15
  Bit_Extender #(.in_width(16), .out_width(4), .\type ("zero")) bit_extender_1 (
    .in(operand2), .out(bit_extender_1_out));
  assign controlled_buffer_1_out = decoder_1_out0 ? adder_1_out : 16'bz;  // Controlled_Buffer controlled_buffer_1
  Adder #(.width(16)) adder_1 (.a(operand1), .b(operand2), .out(adder_1_out), .cout(adder_1_cout));  // open: cin
  assign controlled_buffer_2_out = decoder_1_out0 ? adder_1_cout : 1'bz;  // Controlled_Buffer controlled_buffer_2
  assign controlled_buffer_1_out = decoder_1_out1 ? subtractor_1_out : 16'bz;  // Controlled_Buffer controlled_buffer_3
  Subtractor #(.width(16)) subtractor_1 (
    .a(operand1), .b(operand2), .out(subtractor_1_out), .bout(subtractor_1_bout));  // open: bin
  assign controlled_buffer_2_out = decoder_1_out1 ? subtractor_1_bout : 1'bz;  // Controlled_Buffer controlled_buffer_4
  assign controlled_buffer_1_out = decoder_1_out2 ? multiplier_1_out : 16'bz;  // Controlled_Buffer controlled_buffer_5
  Multiplier #(.width(16)) multiplier_1 (.a(operand1), .b(operand2), .out(multiplier_1_out));  // open: cin, cout
  assign controlled_buffer_1_out = decoder_1_out3 ? divider_1_out : 16'bz;  // Controlled_Buffer controlled_buffer_6
  Divider #(.width(16)) divider_1 (
    .a(operand1), .b(operand2), .out(divider_1_out), .rem(divider_1_rem));  // open: upper
  assign controlled_buffer_1_out = decoder_1_out4 ? divider_1_rem : 16'bz;  // Controlled_Buffer controlled_buffer_7
  assign and_1_out = operand1 & operand2;  // AND_Gate and_1, 16 bits wide
  assign controlled_buffer_1_out = decoder_1_out5 ? and_1_out : 16'bz;  // Controlled_Buffer controlled_buffer_8
  assign or_1_out = operand1 | operand2;  // OR_Gate or_1, 16 bits wide
  assign controlled_buffer_1_out = decoder_1_out6 ? or_1_out : 16'bz;  // Controlled_Buffer controlled_buffer_9
  assign controlled_buffer_1_out = decoder_1_out7 ? shifter_1_out : 16'bz;  // Controlled_Buffer controlled_buffer_10
  Shifter #(.shift("lr"), .width(16)) shifter_1 (.in(operand1), .\dist (bit_extender_1_out), .out(shifter_1_out));
  assign controlled_buffer_1_out = decoder_1_out8 ? shifter_2_out : 16'bz;  // Controlled_Buffer controlled_buffer_11
  Shifter #(.width(16)) shifter_2 (.in(operand1), .\dist (bit_extender_1_out), .out(shifter_2_out));
  assign not_1_out = ~operand1;  // NOT_Gate not_1, 16 bits wide
  assign controlled_buffer_1_out = decoder_1_out9 ? not_1_out : 16'bz;  // Controlled_Buffer controlled_buffer_12
  assign controlled_buffer_1_out = decoder_1_out10 ? negator_1_out : 16'bz;  // Controlled_Buffer controlled_buffer_13
  Negator #(.width(16)) negator_1 (.in(operand1), .out(negator_1_out));
  assign result = ALU_enable ? controlled_buffer_1_out : 16'bz;  // Controlled_Buffer controlled_buffer_14
  D_Flip_Flop d_ff_1 (.D(controlled_buffer_2_out), .clk(and_2_out), .Q(carry));  // open: Qn, preset, reset
  and and_2 (and_2_out, ALU_enable, CLK);
endmodule

module CMP (
  input  trybranch,
  input  compare,
  input  [7:0] opcode,
  input  [15:0] operand1,
  input  [15:0] operand2,
  input  carry,
  input  port_ready,
  input  CLK,
  output dobranch
);

  wire controlled_buffer_1_out, decoder_1_out0, decoder_1_out1, decoder_1_out2, decoder_1_out3,
       decoder_1_out4, decoder_1_out5, multiplexer_1_out, not_1_out;
  wire [2:0] comparator_1_gt;
  wire [4:0] register_1_q;

  Comparator #(.mode("unsigned"), .width(16)) comparator_1 (
    .a(operand1), .b(operand2), .gt(comparator_1_gt[0]), .eq(comparator_1_gt[1]), .lt(comparator_1_gt[2]));
  Register #(.width(5)) register_1 (
    .D({port_ready, carry, comparator_1_gt}), .en(compare), .clk(CLK), .Q(register_1_q));  // open: clr
  Decoder #(.enable("false"), .select(3)) decoder_1 (
    .out0(decoder_1_out0), .out1(decoder_1_out1), .out2(decoder_1_out2), .out3(decoder_1_out3),
    .out4(decoder_1_out4), .out5(decoder_1_out5), .sel(opcode[3:1]));  // open: out6, out7
  assign controlled_buffer_1_out = decoder_1_out1 ? register_1_q[0] : 1'bz;  // Controlled_Buffer controlled_buffer_1
  assign controlled_buffer_1_out = decoder_1_out0 ? register_1_q[1] : 1'bz;  // Controlled_Buffer controlled_buffer_2
  assign controlled_buffer_1_out = decoder_1_out2 ? register_1_q[2] : 1'bz;  // Controlled_Buffer controlled_buffer_3
  assign controlled_buffer_1_out = decoder_1_out3 ? register_1_q[3] : 1'bz;  // Controlled_Buffer controlled_buffer_4
  assign controlled_buffer_1_out = decoder_1_out4 ? register_1_q[4] : 1'bz;  // Controlled_Buffer controlled_buffer_5
  assign controlled_buffer_1_out = decoder_1_out5 ? 1'b1 : 1'bz;  // Controlled_Buffer controlled_buffer_6
  Multiplexer multiplexer_1 (.in0(controlled_buffer_1_out), .in1(not_1_out), .out(multiplexer_1_out), .sel(opcode[0]));
  not not_1 (not_1_out, controlled_buffer_1_out);
  and and_1 (dobranch, trybranch, multiplexer_1_out);
endmodule
